# Fritzing sketch Esquematico 1 Tira (saved by Fritzing 1.0.0rc)

parts:
  U1 = WS2812 RGB LED strip
  VCC1 = 4 x AAA Battery Mount
  J1 = Camdenboss CTB0158-3 [part_number=CTB0158-3 package=THT]

nets:
  N1: U1.GND, VCC1.-, J1.pin3
  N2: U1.VCC, VCC1.+, J1.pin1
  N3: U1.DIN, J1.pin2

notes:
  Fuente De Poder
  5V/45W/9A
  WS2812B Driver

custom parts:
  WS2812 RGB LED strip: WS2812 strip
