# Fritzing sketch Esquematico 2 Tiras (saved by Fritzing 1.0.0rc)

parts:
  U1 = WS2812 RGB LED strip
  VCC1 = 4 x AAA Battery Mount
  J1 = Camdenboss CTB0158-3 [part_number=CTB0158-3 package=THT]
  U2 = WS2812 RGB LED strip
  VCC2 = 4 x AAA Battery Mount

nets:
  N1: U1.GND#0, VCC1.-, J1.pin3
  N2: U1.VCC#1, VCC1.+, J1.pin1
  N3: U1.DIN, J1.pin2
  N4: U1.GND#4, U2.GND, VCC2.-
  N5: U1.VCC#5, U2.VCC, VCC2.+
  N6: U1.DOUT, U2.DIN

notes:
  Fuente De Poder
  5V/45W/9A
  WS2812B Driver

custom parts:
  WS2812 RGB LED strip: WS2812 strip
